# Fritzing sketch FritzingDiagram (saved by Fritzing 0.9.4)
breadboards: 2

parts:
  Part1 = Arduino Mega 2560 (Rev3)
  S1 = Pushbutton [package="[THT]"]
  R1 = Temperature Sensor (Thermistor) [thermistor_type=NTC package=THT]
  R2 = Resistor [tolerance=±5% resistance=4.7k package=THT]
  R3 = PHOTOCELL [package=photocell-kit]
  R4 = Resistor [tolerance=±5% resistance=4.7k package=THT]
  Part2 = InvenSense MPU6050

nets:
  N1: Part1.A0, S1.Pin_1, S1.Pin_2
  N2: Part1.A1, R1.pin_1, R2.Pin_0
  N3: Part1.A2, R3.P$2, R4.Pin_0
  N4: Part1.D21/SCL, Part2.SCL
  N5: Part1.D20/SDA, Part2.SDA
  5V: Part1.5V, S1.Pin_3, S1.Pin_4, R1.pin_0, R3.P$1, Part2.VCC
  GND: Part1.GND, R2.Pin_1, R4.Pin_1, Part2.GND
